// Logisim project Projeto Arq. Comp (07.04).circ as structural Verilog: 14 circuits, main circuit main
module main (
  input  E,
  input  [3:0] OPERANDO,
  input  [2:0] UPCODE,
  input  D,
  input  in_5,
  output Overflow,
  output _0
);

  wire clock_1_out, clock_2_out;
  wire [3:0] ac_1_s, mux_1_s, ram_1_data, ula_1_out_6;

  // Probe on ac_1_s
  // Probe on UPCODE
  ULA ula_1 (.D(D), .B(mux_1_s), .A(ac_1_s), .Overflow(Overflow), .in_4(UPCODE), .out_6(ula_1_out_6), ._0(_0));
  Clock clock_1 (.out(clock_1_out));
  AC ac_1 (.Clock(clock_1_out), .E(ula_1_out_6), .S(ac_1_s));
  MUX mux_1 (.E(OPERANDO), .C(E), .D(ram_1_data), .S(mux_1_s));
  // Probe on ula_1_out_6
  // Probe on ram_1_data
  Clock clock_2 (.out(clock_2_out));
  RAM #(.addrWidth(4), .dataWidth(4)) ram_1 (
    .addr(OPERANDO), .data(ram_1_data), .clk(clock_2_out), .ld(in_5));  // open: sel, clr

  // Notes on the sheet:
  //   0
  //   1
  //   2
  //   3
  //   4
  //   5
  //   6
  //   7
  //   8
  //   9
  //   A
  //   B
  //   C
  //   D
  //   E
  //   F
  //   Instruction Set
  //   0
  //   MOV
  //   000
  //   1
  //   000
  //   MOV
  //   0
  //   001
  //   ADD
  //   1
  //   001
  //   ADD
  //   SUB
  //   010
  //   0
  //   1
  //   010
  //   SUB
  //   0
  //   011
  //   OR
  //   1
  //   OR
  //   011
  //   0
  //   NOT
  //   100
  //   100
  //   1
  //   NOT
  //   0
  //   101
  //   SHF
  //   1
  //   SHF
  //   101
  //   0
  //   110
  //   JPZ
  //   JPO
  //   110
  //   1
  //   111
  //   0
  //   GO
  //   STR
  //   1
  //   111
  //   AC <= X
  //   AC <= M(X)
  //   AC <= AC+X
  //   AC <= AC+M(X)
  //   AC <= AC-X
  //   AC <= AC-M(X)
  //   AC <= AC OR X
  //   AC <= AC OR M(X)
  //   AC <= NOT X
  //   AC <= NOT M( X)
  //   AC <= AC << Q
  //   AC <= AC >> Q
  //   PC <= X SE FLAG Z
  //   PC <= X SE FLAG O
  //   PC <= X
  //   M(X) <= AC 
endmodule

module add_1 (
  input  a,
  input  b,
  input  c,
  output S,
  output Vai_1
);

  wire and_1_out, and_2_out, or_1_out, xor_1_out;

  or or_1 (or_1_out, b, c);
  xor xor_1 (xor_1_out, b, c);
  and and_1 (and_1_out, or_1_out, a);
  and and_2 (and_2_out, b, c);
  xor xor_2 (S, a, xor_1_out);
  or or_2 (Vai_1, and_1_out, and_2_out);
endmodule

module add_4 (
  input  [3:0] B,
  input  [3:0] A,
  output Overflow,
  output [3:0] out_4
);

  wire add_1_2_vai_1, add_1_3_vai_1, add_1_4_vai_1;

  // Probe on A
  add_1 add_1_1 (.a(A[3]), .b(B[3]), .c(add_1_2_vai_1), .S(out_4[3]), .Vai_1(Overflow));
  add_1 add_1_2 (.a(A[2]), .b(B[2]), .c(add_1_3_vai_1), .S(out_4[2]), .Vai_1(add_1_2_vai_1));
  add_1 add_1_3 (.a(A[1]), .b(B[1]), .c(add_1_4_vai_1), .S(out_4[1]), .Vai_1(add_1_3_vai_1));
  add_1 add_1_4 (.a(A[0]), .b(B[0]), .c(1'b0), .S(out_4[0]), .Vai_1(add_1_4_vai_1));
  // Probe on out_4
  // Probe on B
endmodule

module sub_1 (
  input  A,
  input  B,
  input  C,
  output A_2,
  output Vai_1
);

  wire and_1_out, and_2_out, or_1_out, xor_1_out;

  xor xor_1 (xor_1_out, C, B);
  or or_1 (or_1_out, C, B);
  xor xor_2 (A_2, xor_1_out, A);
  and and_1 (and_1_out, or_1_out, ~A);  // AND_Gate
  and and_2 (and_2_out, C, B);
  or or_2 (Vai_1, and_1_out, and_2_out);
endmodule

module sub_4 (
  input  [3:0] B,
  input  [3:0] A,
  output out_3,
  output [3:0] out_4
);

  wire sub_1_2_vai_1, sub_1_3_vai_1, sub_1_4_vai_1;

  // Probe on A
  sub_1 sub_1_1 (.A_2(out_4[3]), .Vai_1(out_3), .A(A[3]), .B(B[3]), .C(sub_1_2_vai_1));
  sub_1 sub_1_2 (.A_2(out_4[2]), .Vai_1(sub_1_2_vai_1), .A(A[2]), .B(B[2]), .C(sub_1_3_vai_1));
  sub_1 sub_1_3 (.A_2(out_4[1]), .Vai_1(sub_1_3_vai_1), .A(A[1]), .B(B[1]), .C(sub_1_4_vai_1));
  sub_1 sub_1_4 (.A_2(out_4[0]), .Vai_1(sub_1_4_vai_1), .A(A[0]), .B(B[0]), .C(1'b0));
  // Probe on out_4
  // Probe on B
endmodule

module rot_esq (
  input  [3:0] abcd,
  input  [1:0] xy,
  output [3:0] ABCD_2
);

  wire and_1_out, and_2_out, and_3_out, and_4_out, and_5_out, and_6_out, and_7_out, and_8_out, and_9_out;

  and and_1 (and_1_out, ~xy[1], ~xy[0], abcd[3]);  // AND_Gate
  and and_2 (and_2_out, ~xy[1], xy[0], abcd[2]);  // AND_Gate
  and and_3 (and_3_out, xy[1], ~xy[0], abcd[1]);  // AND_Gate
  and and_4 (and_4_out, xy[1], xy[0], abcd[0]);
  and and_5 (and_5_out, ~xy[1], ~xy[0], abcd[2]);  // AND_Gate
  and and_6 (and_6_out, ~xy[1], xy[0], abcd[1]);  // AND_Gate
  and and_7 (and_7_out, xy[1], ~xy[0], abcd[0]);  // AND_Gate
  and and_8 (and_8_out, ~xy[1], ~xy[0], abcd[1]);  // AND_Gate
  and and_9 (and_9_out, ~xy[1], xy[0], abcd[0]);  // AND_Gate
  and and_10 (ABCD_2[0], ~xy[1], ~xy[0], abcd[0]);  // AND_Gate
  or or_1 (ABCD_2[3], and_1_out, and_2_out, and_3_out, and_4_out);
  or or_2 (ABCD_2[2], and_5_out, and_6_out, and_7_out);
  or or_3 (ABCD_2[1], and_8_out, and_9_out);
endmodule

module rot_dir (
  input  [3:0] abcd,
  input  [1:0] xy,
  output [3:0] ABCD_2
);

  wire and_1_out, and_2_out, and_3_out, and_4_out, and_5_out, and_6_out, and_7_out, and_8_out, and_9_out;

  and and_1 (and_1_out, ~xy[1], ~xy[0], abcd[0]);  // AND_Gate
  and and_2 (and_2_out, ~xy[1], xy[0], abcd[1]);  // AND_Gate
  and and_3 (and_3_out, xy[1], ~xy[0], abcd[2]);  // AND_Gate
  and and_4 (and_4_out, xy[1], xy[0], abcd[3]);
  and and_5 (and_5_out, ~xy[1], ~xy[0], abcd[1]);  // AND_Gate
  and and_6 (and_6_out, ~xy[1], xy[0], abcd[2]);  // AND_Gate
  and and_7 (and_7_out, xy[1], ~xy[0], abcd[3]);  // AND_Gate
  and and_8 (and_8_out, ~xy[1], ~xy[0], abcd[2]);  // AND_Gate
  and and_9 (and_9_out, ~xy[1], xy[0], abcd[3]);  // AND_Gate
  and and_10 (ABCD_2[3], ~xy[1], ~xy[0], abcd[3]);  // AND_Gate
  or or_1 (ABCD_2[0], and_1_out, and_2_out, and_3_out, and_4_out);
  or or_2 (ABCD_2[1], and_5_out, and_6_out, and_7_out);
  or or_3 (ABCD_2[2], and_8_out, and_9_out);
endmodule

module dec_3x8 (
  input  [2:0] in_1,
  output s0,
  output s1,
  output s2,
  output s3,
  output s4,
  output s5,
  output s6,
  output s7
);

  wire not_1_out, not_2_out, not_3_out, not_4_out, not_5_out, not_6_out, not_7_out, not_8_out, not_9_out,
       not_10_out, not_11_out, not_12_out;

  not not_1 (not_1_out, in_1[2]);
  not not_2 (not_2_out, in_1[1]);
  not not_3 (not_3_out, in_1[0]);
  not not_4 (not_4_out, in_1[2]);
  not not_5 (not_5_out, in_1[1]);
  not not_6 (not_6_out, in_1[2]);
  not not_7 (not_7_out, in_1[0]);
  not not_8 (not_8_out, in_1[2]);
  not not_9 (not_9_out, in_1[1]);
  not not_10 (not_10_out, in_1[0]);
  not not_11 (not_11_out, in_1[1]);
  not not_12 (not_12_out, in_1[0]);
  and and_1 (s7, in_1[2], in_1[1], in_1[0]);
  and and_2 (s0, not_1_out, not_2_out, not_3_out);
  and and_3 (s1, not_4_out, not_5_out, in_1[0]);
  and and_4 (s2, not_6_out, in_1[1], not_7_out);
  and and_5 (s3, not_8_out, in_1[1], in_1[0]);
  and and_6 (s4, in_1[2], not_9_out, not_10_out);
  and and_7 (s5, in_1[2], not_11_out, in_1[0]);
  and and_8 (s6, in_1[2], in_1[1], not_12_out);
endmodule

module buffer (
  input  [3:0] E,
  input  in_2,
  output [3:0] S
);

  assign S[2] = in_2 ? E[2] : 1'bz;  // Controlled_Buffer controlled_buffer_1
  assign S[3] = in_2 ? E[3] : 1'bz;  // Controlled_Buffer controlled_buffer_2
  assign S[1] = in_2 ? E[1] : 1'bz;  // Controlled_Buffer controlled_buffer_3
  assign S[0] = in_2 ? E[0] : 1'bz;  // Controlled_Buffer controlled_buffer_4
endmodule

module or_4bits (
  input  [3:0] B,
  input  [3:0] A,
  output [3:0] out_3
);

  // Probe on A
  or or_1 (out_3[3], A[3], B[3]);
  or or_2 (out_3[2], A[2], B[2]);
  or or_3 (out_3[1], A[1], B[1]);
  or or_4 (out_3[0], A[0], B[0]);
  // Probe on out_3
  // Probe on B
endmodule

module buff_4bits (
  input  [3:0] E,
  output [3:0] S
);

  not not_1 (S[2], E[2]);
  not not_2 (S[3], E[3]);
  not not_3 (S[0], E[0]);
  not not_4 (S[1], E[1]);
endmodule

module ULA (
  input  D,
  input  [3:0] B,
  input  [3:0] A,
  input  [2:0] in_4,
  output Overflow,
  output [3:0] out_6,
  output _0
);

  wire add_4_1_overflow, and_1_out, and_2_out, dec_3x8_1_s0, dec_3x8_1_s1, dec_3x8_1_s2, dec_3x8_1_s3,
       dec_3x8_1_s4, dec_3x8_1_s5, dec_3x8_1_s6, dec_3x8_1_s7, not_1_out, sub_4_1_out_3;
  wire [3:0] add_4_1_out_4, buff_4bits_1_s, buffer_6_s, or_4bits_1_out_3, rot_dir_1_abcd_2, rot_esq_1_abcd_2,
       sub_4_1_out_4;

  or or_1 (Overflow, and_1_out, and_2_out);
  dec_3x8 dec_3x8_1 (
    .in_1(in_4), .s0(dec_3x8_1_s0), .s1(dec_3x8_1_s1), .s2(dec_3x8_1_s2), .s3(dec_3x8_1_s3),
    .s4(dec_3x8_1_s4), .s5(dec_3x8_1_s5), .s6(dec_3x8_1_s6), .s7(dec_3x8_1_s7));
  and and_1 (and_1_out, add_4_1_overflow, dec_3x8_1_s1);
  and and_2 (and_2_out, sub_4_1_out_3, dec_3x8_1_s2);
  buffer buffer_1 (.E(B), .in_2(dec_3x8_1_s0), .S(out_6));
  add_4 add_4_1 (.A(A), .Overflow(add_4_1_overflow), .B(B), .out_4(add_4_1_out_4));
  buffer buffer_2 (.E(add_4_1_out_4), .in_2(dec_3x8_1_s1), .S(out_6));
  sub_4 sub_4_1 (.A(A), .B(B), .out_4(sub_4_1_out_4), .out_3(sub_4_1_out_3));
  buffer buffer_3 (.E(sub_4_1_out_4), .in_2(dec_3x8_1_s2), .S(out_6));
  // Probe on out_6
  nor nor_1 (_0, out_6[0], out_6[1], out_6[2], out_6[3], dec_3x8_1_s6, dec_3x8_1_s7);
  buff_4bits buff_4bits_1 (.E(B), .S(buff_4bits_1_s));
  or_4bits or_4bits_1 (.A(A), .B(B), .out_3(or_4bits_1_out_3));
  buffer buffer_4 (.E(or_4bits_1_out_3), .in_2(dec_3x8_1_s3), .S(out_6));
  buffer buffer_5 (.E(buff_4bits_1_s), .in_2(dec_3x8_1_s4), .S(out_6));
  rot_esq rot_esq_1 (.abcd(A), .xy(B[1:0]), .ABCD_2(rot_esq_1_abcd_2));
  rot_dir rot_dir_1 (.abcd(A), .xy(B[1:0]), .ABCD_2(rot_dir_1_abcd_2));
  not not_1 (not_1_out, D);
  buffer buffer_6 (.E(rot_esq_1_abcd_2), .in_2(not_1_out), .S(buffer_6_s));
  buffer buffer_7 (.E(rot_dir_1_abcd_2), .in_2(D), .S(buffer_6_s));
  buffer buffer_8 (.E(buffer_6_s), .in_2(dec_3x8_1_s5), .S(out_6));
endmodule

module AC (
  input  Clock,
  input  [3:0] E,
  output [3:0] S
);

  D_Flip_Flop D3 (.clk(Clock), .D(E[3]), .Q(S[3]));  // open: Qn, preset, en, reset
  D_Flip_Flop D2 (.clk(Clock), .D(E[2]), .Q(S[2]));  // open: Qn, preset, en, reset
  D_Flip_Flop D1 (.clk(Clock), .D(E[1]), .Q(S[1]));  // open: Qn, preset, en, reset
  D_Flip_Flop D0 (.clk(Clock), .D(E[0]), .Q(S[0]));  // open: Qn, preset, en, reset
endmodule

module MUX (
  input  [3:0] E,
  input  [3:0] D,
  input  C,
  output [3:0] S
);

  wire not_1_out;

  not not_1 (not_1_out, C);
  buffer buffer_1 (.E(E), .in_2(not_1_out), .S(S));
  buffer buffer_2 (.E(D), .in_2(C), .S(S));
endmodule
