// Logisim project Projeto Arq. Comp (10.02).circ as structural Verilog: 2 circuits, main circuit main
module main (
  input  b,
  input  b_2,
  input  b_3,
  input  b_4,
  input  a,
  input  a_2,
  input  a_3,
  input  a_4,
  input  in_9,
  output Vai_1,
  output out_11,
  output out_12,
  output out_13,
  output out_14
);

  wire add_1_2_vai_1, add_1_3_vai_1, add_1_4_vai_1;

  add_1 add_1_1 (.a(b), .b(a), .c(add_1_2_vai_1), .S(out_11), .Vai_1(Vai_1));
  add_1 add_1_2 (.a(b_2), .b(a_2), .c(add_1_3_vai_1), .S(out_12), .Vai_1(add_1_2_vai_1));
  add_1 add_1_3 (.a(b_3), .b(a_3), .c(add_1_4_vai_1), .S(out_13), .Vai_1(add_1_3_vai_1));
  add_1 add_1_4 (.a(b_4), .b(a_4), .c(in_9), .S(out_14), .Vai_1(add_1_4_vai_1));
endmodule

// Add_1
module add_1 (
  input  a,
  input  b,
  input  c,
  output S,
  output Vai_1
);

  wire and_1_out, and_2_out, or_1_out, xor_1_out;

  or or_1 (or_1_out, b, c);
  xor xor_1 (xor_1_out, b, c);
  and and_1 (and_1_out, or_1_out, a);
  and and_2 (and_2_out, b, c);
  xor xor_2 (S, a, xor_1_out);
  or or_2 (Vai_1, and_1_out, and_2_out);
endmodule
