// Logisim project Tabela Bizu.circ as structural Verilog: 1 circuit, main circuit main
module main (
);


  // Notes on the sheet:
  //   0
  //   1
  //   2
  //   3
  //   4
  //   5
  //   6
  //   7
  //   8
  //   9
  //   A
  //   B
  //   C
  //   D
  //   E
  //   F
  //   Instruction Set
  //   0
  //   000
  //   MOV
  //   1
  //   000
  //   MOV
  //   0
  //   001
  //   ADD
  //   1
  //   001
  //   ADD
  //   010
  //   0
  //   SUB
  //   1
  //   010
  //   SUB
  //   0
  //   011
  //   OR
  //   1
  //   OR
  //   011
  //   0
  //   100
  //   NOT
  //   100
  //   NOT
  //   1
  //   101
  //   0
  //   SHF
  //   1
  //   SHF
  //   101
  //   JPZ
  //   0
  //   110
  //   JPO
  //   110
  //   1
  //   0
  //   111
  //   GO
  //   STR
  //   1
  //   111
  //   AC <= X
  //   AC <= M(X)
  //   AC <= AC+X
  //   AC <= AC+M(X)
  //   AC <= AC-X
  //   AC <= AC-M(X)
  //   AC <= AC OR X
  //   AC <= AC OR M(X)
  //   AC <= NOT X
  //   AC <= NOT M( X)
  //   AC <= AC << Q
  //   AC <= AC >> Q
  //   PC <= X SE FLAG Z
  //   PC <= X SE FLAG O
  //   PC <= X
  //   M(X) <= AC 
endmodule
