// Logisim project BCD_Circuito_E_doBlog.circ as structural Verilog
module circuitoBCD (
  input  in_1,
  input  in_2,
  input  in_3,
  input  in_4
);

  wire clock_1_out, entradas_saidas_1_out_5, entradas_saidas_1_out_6, entradas_saidas_1_out_7,
       entradas_saidas_1_out_8, entradas_saidas_1_out_9, entradas_saidas_1_out_10, entradas_saidas_1_out_11,
       entradas_saidas_2_out_5, entradas_saidas_2_out_6, entradas_saidas_2_out_7, entradas_saidas_2_out_8,
       entradas_saidas_2_out_9, entradas_saidas_2_out_10, entradas_saidas_2_out_11;
  wire [3:0] counter_1_q;

  Counter #(.width(4), .max('hf)) counter_1 (.Q(counter_1_q), .clk(clock_1_out));  // open: load, D, count, carry, clr
  Clock clock_1 (.out(clock_1_out));
  Entradas_saidas entradas_saidas_1 (
    .A(in_1), .B(in_2), .C(in_3), .D(in_4), .out_5(entradas_saidas_1_out_5), .out_6(entradas_saidas_1_out_6),
    .out_7(entradas_saidas_1_out_7), .out_8(entradas_saidas_1_out_8), .out_9(entradas_saidas_1_out_9),
    .out_10(entradas_saidas_1_out_10), .out_11(entradas_saidas_1_out_11));
  _7_Segment_Display u_7_segment_display_1 (
    .g(entradas_saidas_1_out_11), .f(entradas_saidas_1_out_10), .a(entradas_saidas_1_out_5),
    .b(entradas_saidas_1_out_6), .e(entradas_saidas_1_out_9), .d(entradas_saidas_1_out_8),
    .c(entradas_saidas_1_out_7));  // open: dp
  Entradas_saidas entradas_saidas_2 (
    .A(counter_1_q[3]), .B(counter_1_q[2]), .C(counter_1_q[1]), .D(counter_1_q[0]),
    .out_5(entradas_saidas_2_out_5), .out_6(entradas_saidas_2_out_6), .out_7(entradas_saidas_2_out_7),
    .out_8(entradas_saidas_2_out_8), .out_9(entradas_saidas_2_out_9), .out_10(entradas_saidas_2_out_10),
    .out_11(entradas_saidas_2_out_11));
  _7_Segment_Display u_7_segment_display_2 (
    .g(entradas_saidas_2_out_11), .f(entradas_saidas_2_out_10), .a(entradas_saidas_2_out_5),
    .b(entradas_saidas_2_out_6), .e(entradas_saidas_2_out_9), .d(entradas_saidas_2_out_8),
    .c(entradas_saidas_2_out_7));  // open: dp
endmodule

module Entradas_saidas (
  input  A,
  input  B,
  input  C,
  input  D,
  output out_5,
  output out_6,
  output out_7,
  output out_8,
  output out_9,
  output out_10,
  output out_11
);

  wire and_1_out, and_2_out, and_3_out, and_5_out, and_6_out, and_7_out, or_1_out, or_2_out, or_3_out,
       xnor_1_out, xnor_2_out, xor_1_out;

  xnor xnor_1 (xnor_1_out, B, D);
  xnor xnor_2 (xnor_2_out, C, D);
  and and_1 (and_1_out, B, ~C, D);  // AND_Gate
  and and_2 (and_2_out, ~D, C);  // AND_Gate
  or or_1 (or_1_out, C, ~D);  // OR_Gate
  and and_3 (and_3_out, or_1_out, ~B);  // AND_Gate
  or or_2 (or_2_out, C, ~B);  // OR_Gate
  and and_4 (out_9, or_2_out, ~D);  // AND_Gate
  and and_5 (and_5_out, or_3_out, B);
  or or_3 (or_3_out, ~D, ~C);  // OR_Gate
  and and_6 (and_6_out, ~C, ~D);  // AND_Gate
  xor xor_1 (xor_1_out, B, C);
  or or_4 (out_11, xor_1_out, and_7_out, A);
  and and_7 (and_7_out, C, ~D);  // AND_Gate
  or or_5 (out_5, A, xnor_1_out, C);
  or or_6 (out_6, ~B, xnor_2_out);  // OR_Gate
  or or_7 (out_7, B, ~C, D);  // OR_Gate
  or or_8 (out_8, A, and_1_out, and_2_out, and_3_out);
  or or_9 (out_10, and_5_out, and_6_out, A);
endmodule

module bcd_do_blog (
  input  A,
  input  B,
  input  C,
  output out_4,
  output out_5,
  output out_6,
  output out_7,
  output out_8,
  output out_9,
  output out_10
);

  wire and_3_out, or_1_out;

  or or_1 (or_1_out, B, C);
  and and_1 (out_9, A, B);
  and and_2 (out_10, A, B, C);
  or or_2 (out_4, A, B, C);
  or or_3 (out_5, A, B);
  and and_3 (and_3_out, B, C);
  or or_4 (out_6, and_3_out, A);
  and and_4 (out_8, or_1_out, A);

  assign out_7 = A;
endmodule

module TESTE_BCD_DO_BLOG (
  input  in_1,
  input  in_2,
  input  in_3
);

  wire bcd_do_blog_1_out_4, bcd_do_blog_1_out_5, bcd_do_blog_1_out_6, bcd_do_blog_1_out_7,
       bcd_do_blog_1_out_8, bcd_do_blog_1_out_9, bcd_do_blog_1_out_10;

  LED led_1 (.in(bcd_do_blog_1_out_4));
  bcd_do_blog bcd_do_blog_1 (
    .out_4(bcd_do_blog_1_out_4), .out_5(bcd_do_blog_1_out_5), .out_6(bcd_do_blog_1_out_6),
    .out_7(bcd_do_blog_1_out_7), .out_8(bcd_do_blog_1_out_8), .out_9(bcd_do_blog_1_out_9),
    .out_10(bcd_do_blog_1_out_10), .A(in_1), .B(in_2), .C(in_3));
  LED led_2 (.in(bcd_do_blog_1_out_6));
  LED led_3 (.in(bcd_do_blog_1_out_5));
  LED led_4 (.in(bcd_do_blog_1_out_7));
  LED led_5 (.in(bcd_do_blog_1_out_10));
  LED led_6 (.in(bcd_do_blog_1_out_9));
  LED led_7 (.in(bcd_do_blog_1_out_8));
endmodule
