// Logisim project Circuito Expressão.circ as structural Verilog
module \circuito_expressão  (
  input  A,
  input  B,
  input  C,
  input  D,
  output out_5
);

  wire and_1_out, nand_1_out, nor_1_out, nor_2_out, not_1_out, not_2_out, not_3_out, not_4_out, or_1_out,
       xnor_1_out;

  not not_1 (not_1_out, A);
  not not_2 (not_2_out, C);
  not not_3 (not_3_out, D);
  not not_4 (not_4_out, D);
  or or_1 (or_1_out, A, not_4_out);
  nor nor_1 (nor_1_out, B, C);
  xnor xnor_1 (xnor_1_out, not_1_out, B);
  and and_1 (and_1_out, not_2_out, not_3_out);
  nor nor_2 (nor_2_out, xnor_1_out, and_1_out);
  nand nand_1 (nand_1_out, or_1_out, nor_1_out);
  xnor xnor_2 (out_5, nor_2_out, nand_1_out);
endmodule
