// Logisim project Circuito Lógico 1.1.circ as structural Verilog: 2 circuits, main circuit main
module main (
  input  A,
  input  B,
  input  Vem_1,
  output S,
  output Vai_1
);

  wire and_1_out, and_2_out, or_1_out, xor_1_out;

  xor xor_1 (xor_1_out, B, A);
  or or_1 (or_1_out, Vem_1, B);
  and and_1 (and_1_out, B, Vem_1);
  xor xor_2 (S, Vem_1, xor_1_out);
  and and_2 (and_2_out, or_1_out, A);
  or or_2 (Vai_1, and_2_out, and_1_out);
endmodule

module add_4 (
  input  [5:0] in_1,
  input  [3:0] A,
  input  [3:0] A_2,
  output Overflow
);

  wire main_1_s, main_1_vai_1, main_2_s, main_2_vai_1, main_3_s, main_3_vai_1, main_4_s, main_4_vai_1,
       undriven_2, undriven_3, undriven_4, undriven_5;
  wire [1:0] undriven, undriven_6;

  _7_Segment_Display u_7_segment_display_1 ();  // open: g, f, a, b, e, d, c, dp
  main main_1 (.S(main_1_s), .Vai_1(main_1_vai_1), .A(undriven_3), .B(undriven_4), .Vem_1(Overflow));
  main main_2 (.S(main_2_s), .Vai_1(main_2_vai_1), .A(undriven_2), .B(undriven_5), .Vem_1(main_1_vai_1));
  main main_3 (.S(main_3_s), .Vai_1(main_3_vai_1), .A(undriven[1]), .B(undriven_6[1]), .Vem_1(main_2_vai_1));
  main main_4 (.S(main_4_s), .Vai_1(main_4_vai_1), .A(undriven[0]), .B(undriven_6[0]), .Vem_1(main_3_vai_1));
  _7_Segment_Display u_7_segment_display_2 ();  // open: g, f, a, b, e, d, c, dp
  // also tied to GND on the sheet: main_4_vai_1
endmodule
