// Logisim project Circuito_Subtração.circ as structural Verilog: 5 circuits, main circuit main
module main (
  input  [3:0] in_1,
  output [3:0] out_2
);

  // Probe on out_2
  // Probe on in_1
  Comp_2 comp_2_1 (.in_1(in_1), .out_3(out_2));  // open: vai_1
endmodule

module Add_1 (
  input  A,
  input  B,
  input  Vem_1,
  output S,
  output Vai_1
);

  wire and_1_out, and_2_out, or_1_out, xor_1_out;

  xor xor_1 (xor_1_out, A, B);
  or or_1 (or_1_out, B, Vem_1);
  and and_1 (and_1_out, or_1_out, A);
  and and_2 (and_2_out, B, Vem_1);
  xor xor_2 (S, xor_1_out, Vem_1);
  or or_2 (Vai_1, and_1_out, and_2_out);
endmodule

module Add_4 (
  input  [3:0] in_1,
  input  [3:0] in_2,
  output overflow,
  output [3:0] out_4
);

  wire add_1_2_vai_1, add_1_3_vai_1, add_1_4_vai_1;

  // Probe on in_2
  Add_1 add_1_1 (.S(out_4[3]), .Vai_1(overflow), .A(in_2[3]), .B(in_1[3]), .Vem_1(add_1_2_vai_1));
  Add_1 add_1_2 (.S(out_4[2]), .Vai_1(add_1_2_vai_1), .A(in_2[2]), .B(in_1[2]), .Vem_1(add_1_3_vai_1));
  Add_1 add_1_3 (.S(out_4[1]), .Vai_1(add_1_3_vai_1), .A(in_2[1]), .B(in_1[1]), .Vem_1(add_1_4_vai_1));
  Add_1 add_1_4 (.S(out_4[0]), .Vai_1(add_1_4_vai_1), .A(in_2[0]), .B(in_1[0]), .Vem_1(1'b0));
  // Probe on out_4
  // Probe on in_1
endmodule

module Comp_2 (
  input  [3:0] in_1,
  output vai_1,
  output [3:0] out_3
);

  wire [3:0] not_3_out;

  not not_1 (not_3_out[3], in_1[3]);
  not not_2 (not_3_out[1], in_1[1]);
  not not_3 (not_3_out[0], in_1[0]);
  not not_4 (not_3_out[2], in_1[2]);
  Add_4 add_4_1 (.overflow(vai_1), .in_1(4'b0001), .out_4(out_3), .in_2(not_3_out));
endmodule

module Sub_1 (
  input  [3:0] in_1,
  input  [3:0] in_2,
  output out_3,
  output out_4,
  output [3:0] out_5
);

  wire [3:0] comp_2_1_out_3;

  // Probe on in_2
  Add_4 add_4_1 (.overflow(out_4), .in_1(comp_2_1_out_3), .out_4(out_5), .in_2(in_2));
  // Probe on out_5
  // Probe on in_1
  Comp_2 comp_2_1 (.in_1(in_1), .vai_1(out_3), .out_3(comp_2_1_out_3));
endmodule
