// Logisim project Expressão S - Simp.circ as structural Verilog
// Expressão S
module circuito (
  input  a,
  input  b,
  input  c,
  input  d,
  output out_5
);

  wire and_1_out, and_2_out;

  and and_1 (and_1_out, d, b);
  and and_2 (and_2_out, c, ~b, a);  // AND_Gate
  or or_1 (out_5, and_1_out, and_2_out);
endmodule

module macro (
  input  in_1,
  input  in_2,
  input  in_3,
  input  in_4,
  output out_5
);

  circuito circuito_1 (.out_5(out_5), .a(in_1), .b(in_2), .c(in_3), .d(in_4));
endmodule
