// Logisim project Expressão S Simp.circ as structural Verilog
// Expressão S
module \Expressão  (
  input  a,
  input  b,
  input  c,
  input  d,
  output out_5
);

  wire and_1_out, and_2_out, and_3_out, and_4_out, or_1_out, or_2_out;

  and and_1 (and_1_out, d, c);
  and and_2 (and_2_out, b, a);
  or or_1 (or_1_out, b, a);
  or or_2 (or_2_out, c, d);
  and and_3 (and_3_out, and_1_out, or_1_out);
  and and_4 (and_4_out, and_2_out, or_2_out);
  or or_3 (out_5, and_3_out, and_4_out);
endmodule

module Mion (
  input  in_1,
  input  in_2,
  input  in_3,
  input  in_4,
  output out_5
);

  \Expressão  \expressão_1  (.a(in_1), .b(in_2), .c(in_3), .d(in_4), .out_5(out_5));
endmodule
