// Logisim project Expressão S Soma.circ as structural Verilog
// Expressão S
module \Expressão  (
  input  a,
  input  b,
  input  c,
  input  d,
  output out_5
);

  wire and_1_out, and_2_out, and_3_out, and_4_out;

  and and_1 (and_1_out, a, b, c);
  and and_2 (and_2_out, a, c, d);
  and and_3 (and_3_out, a, b, d);
  and and_4 (and_4_out, b, c, d);
  or or_1 (out_5, and_1_out, and_2_out, and_3_out, and_4_out);
endmodule

module Mion (
  input  in_1,
  input  in_2,
  input  in_3,
  input  in_4,
  output out_5
);

  \Expressão  \expressão_1  (.a(in_1), .b(in_2), .c(in_3), .d(in_4), .out_5(out_5));
endmodule
