// Logisim project Expressão S.circ as structural Verilog
// Expressão S
module \Expressão  (
  input  a,
  input  b,
  input  c,
  input  d,
  output out_5
);

  wire and_1_out, and_2_out, and_3_out, and_4_out, and_5_out, not_1_out, not_2_out, not_3_out, not_4_out;

  and and_1 (and_1_out, d, c, b, not_1_out);
  not not_1 (not_1_out, a);
  not not_2 (not_2_out, b);
  not not_3 (not_3_out, c);
  not not_4 (not_4_out, d);
  and and_2 (and_2_out, d, c, not_2_out, a);
  and and_3 (and_3_out, d, not_3_out, b, a);
  and and_4 (and_4_out, not_4_out, c, b, a);
  and and_5 (and_5_out, d, c, b, a);
  or or_1 (out_5, and_1_out, and_2_out, and_3_out, and_4_out, and_5_out);
endmodule

module Mion (
  input  in_1,
  input  in_2,
  input  in_3,
  input  in_4,
  output out_5
);

  \Expressão  \expressão_1  (.out_5(out_5), .a(in_1), .b(in_2), .c(in_3), .d(in_4));
endmodule
