// Logisim project Projeto Arq. Comp (24.02).circ as structural Verilog
module add_1 (
  input  a,
  input  b,
  input  c,
  output S,
  output Vai_1
);

  wire and_1_out, and_2_out, or_1_out, xor_1_out;

  or or_1 (or_1_out, b, c);
  xor xor_1 (xor_1_out, b, c);
  and and_1 (and_1_out, or_1_out, a);
  and and_2 (and_2_out, b, c);
  xor xor_2 (S, a, xor_1_out);
  or or_2 (Vai_1, and_1_out, and_2_out);
endmodule

module add_4 (
  input  [3:0] B,
  input  [3:0] A,
  output Overflow,
  output [3:0] out_4
);

  wire add_1_2_vai_1, add_1_3_vai_1, add_1_4_vai_1;

  // Probe on A
  add_1 add_1_1 (.a(A[3]), .b(B[3]), .c(add_1_2_vai_1), .S(out_4[3]), .Vai_1(Overflow));
  add_1 add_1_2 (.a(A[2]), .b(B[2]), .c(add_1_3_vai_1), .S(out_4[2]), .Vai_1(add_1_2_vai_1));
  add_1 add_1_3 (.a(A[1]), .b(B[1]), .c(add_1_4_vai_1), .S(out_4[1]), .Vai_1(add_1_3_vai_1));
  add_1 add_1_4 (.a(A[0]), .b(B[0]), .c(1'b0), .S(out_4[0]), .Vai_1(add_1_4_vai_1));
  // Probe on out_4
  // Probe on B
endmodule

module sub_1 (
  input  A,
  input  B,
  input  C,
  output A_2,
  output Vai_1
);

  wire and_1_out, and_2_out, or_1_out, xor_1_out;

  xor xor_1 (xor_1_out, C, B);
  or or_1 (or_1_out, C, B);
  xor xor_2 (A_2, xor_1_out, A);
  and and_1 (and_1_out, or_1_out, ~A);  // AND_Gate
  and and_2 (and_2_out, C, B);
  or or_2 (Vai_1, and_1_out, and_2_out);
endmodule

module sub_4 (
  input  [3:0] B,
  input  [3:0] A,
  output out_3,
  output [3:0] out_4
);

  wire sub_1_2_vai_1, sub_1_3_vai_1, sub_1_4_vai_1;

  // Probe on A
  sub_1 sub_1_1 (.A_2(out_4[3]), .Vai_1(out_3), .A(A[3]), .B(B[3]), .C(sub_1_2_vai_1));
  sub_1 sub_1_2 (.A_2(out_4[2]), .Vai_1(sub_1_2_vai_1), .A(A[2]), .B(B[2]), .C(sub_1_3_vai_1));
  sub_1 sub_1_3 (.A_2(out_4[1]), .Vai_1(sub_1_3_vai_1), .A(A[1]), .B(B[1]), .C(sub_1_4_vai_1));
  sub_1 sub_1_4 (.A_2(out_4[0]), .Vai_1(sub_1_4_vai_1), .A(A[0]), .B(B[0]), .C(1'b0));
  // Probe on out_4
  // Probe on B
endmodule
