// Logisim project Projeto Arq. Comp..circ as structural Verilog: 2 circuits, main circuit main
module main (
  input  a,
  input  b,
  input  a_2,
  input  b_2,
  input  c,
  input  c_2,
  input  a_3,
  input  b_3,
  input  a_4,
  input  b_4,
  input  c_3,
  input  c_4,
  output Vai_1,
  output Vai_1_2,
  output out_15,
  output out_16,
  output Vai_1_3,
  output Vai_1_4,
  output out_19,
  output out_20
);

  add_1 add_1_1 (.a(b), .b(a), .c(c), .S(out_15), .Vai_1(Vai_1));
  add_1 add_1_2 (.a(b_3), .b(a_3), .c(c_3), .S(out_19), .Vai_1(Vai_1_3));
  add_1 add_1_3 (.a(b_2), .b(a_2), .c(c_2), .S(out_16), .Vai_1(Vai_1_2));
  add_1 add_1_4 (.a(b_4), .b(a_4), .c(c_4), .S(out_20), .Vai_1(Vai_1_4));
endmodule

// Add_1
module add_1 (
  input  a,
  input  b,
  input  c,
  output S,
  output Vai_1
);

  wire and_1_out, and_2_out, or_1_out, xor_1_out;

  or or_1 (or_1_out, b, c);
  xor xor_1 (xor_1_out, b, c);
  and and_1 (and_1_out, or_1_out, a);
  and and_2 (and_2_out, b, c);
  xor xor_2 (S, a, xor_1_out);
  or or_2 (Vai_1, and_1_out, and_2_out);
endmodule
