// Logisim project eletronica (1).circ as structural Verilog
module add_1bit (
  input  A,
  input  B,
  input  Vem_1,
  output S,
  output Vai_1
);

  wire and_1_out, and_2_out, or_1_out, xor_1_out;

  xor xor_1 (xor_1_out, A, B);
  or or_1 (or_1_out, B, Vem_1);
  and and_1 (and_1_out, or_1_out, A);
  and and_2 (and_2_out, B, Vem_1);
  xor xor_2 (S, xor_1_out, Vem_1);
  or or_2 (Vai_1, and_1_out, and_2_out);
endmodule

module add_4 (
  input  [3:0] in_1,
  input  [3:0] in_2,
  output overflow,
  output [3:0] out_4
);

  wire add_1bit_2_vai_1, add_1bit_3_vai_1, add_1bit_4_vai_1;

  // Probe on in_2
  add_1bit add_1bit_1 (.S(out_4[3]), .Vai_1(overflow), .A(in_2[3]), .B(in_1[3]), .Vem_1(add_1bit_2_vai_1));
  add_1bit add_1bit_2 (.S(out_4[2]), .Vai_1(add_1bit_2_vai_1), .A(in_2[2]), .B(in_1[2]), .Vem_1(add_1bit_3_vai_1));
  add_1bit add_1bit_3 (.S(out_4[1]), .Vai_1(add_1bit_3_vai_1), .A(in_2[1]), .B(in_1[1]), .Vem_1(add_1bit_4_vai_1));
  add_1bit add_1bit_4 (.S(out_4[0]), .Vai_1(add_1bit_4_vai_1), .A(in_2[0]), .B(in_1[0]), .Vem_1(1'b0));
  // Probe on out_4
  // Probe on in_1
endmodule
