// Logisim project Projeto Arq. Comp (17.03).circ as structural Verilog: 9 circuits, main circuit main
module main (
  input  [1:0] xy,
  input  [3:0] B,
  input  [3:0] A,
  input  [2:0] in_4,
  output Overflow,
  output Overflow_2,
  output [3:0] out_7
);

  wire dec_3x8_1_s0, dec_3x8_1_s1, dec_3x8_1_s2, dec_3x8_1_s3;
  wire [3:0] add_4_1_out_4, rot_dir_1_abcd_2, rot_esq_1_abcd_2, sub_4_1_out_4;

  dec_3x8 dec_3x8_1 (
    .in_1(in_4), .s0(dec_3x8_1_s0), .s1(dec_3x8_1_s1), .s2(dec_3x8_1_s2), .s3(dec_3x8_1_s3));  // open: s4, s5, s6, s7
  add_4 add_4_1 (.A(A), .Overflow(Overflow), .B(B), .out_4(add_4_1_out_4));
  buffer buffer_1 (.E(add_4_1_out_4), .in_2(dec_3x8_1_s0), .S(out_7));
  sub_4 sub_4_1 (.A(A), .B(B), .out_4(sub_4_1_out_4), .out_3(Overflow_2));
  buffer buffer_2 (.E(sub_4_1_out_4), .in_2(dec_3x8_1_s1), .S(out_7));
  // Probe on out_7
  rot_esq rot_esq_1 (.abcd(A), .xy(xy), .ABCD_2(rot_esq_1_abcd_2));
  rot_dir rot_dir_1 (.abcd(A), .xy(xy), .ABCD_2(rot_dir_1_abcd_2));
  buffer buffer_3 (.E(rot_dir_1_abcd_2), .in_2(dec_3x8_1_s2), .S(out_7));
  buffer buffer_4 (.E(rot_esq_1_abcd_2), .in_2(dec_3x8_1_s3), .S(out_7));
endmodule

module add_1 (
  input  a,
  input  b,
  input  c,
  output S,
  output Vai_1
);

  wire and_1_out, and_2_out, or_1_out, xor_1_out;

  or or_1 (or_1_out, b, c);
  xor xor_1 (xor_1_out, b, c);
  and and_1 (and_1_out, or_1_out, a);
  and and_2 (and_2_out, b, c);
  xor xor_2 (S, a, xor_1_out);
  or or_2 (Vai_1, and_1_out, and_2_out);
endmodule

module add_4 (
  input  [3:0] B,
  input  [3:0] A,
  output Overflow,
  output [3:0] out_4
);

  wire add_1_2_vai_1, add_1_3_vai_1, add_1_4_vai_1;

  // Probe on A
  add_1 add_1_1 (.a(A[3]), .b(B[3]), .c(add_1_2_vai_1), .S(out_4[3]), .Vai_1(Overflow));
  add_1 add_1_2 (.a(A[2]), .b(B[2]), .c(add_1_3_vai_1), .S(out_4[2]), .Vai_1(add_1_2_vai_1));
  add_1 add_1_3 (.a(A[1]), .b(B[1]), .c(add_1_4_vai_1), .S(out_4[1]), .Vai_1(add_1_3_vai_1));
  add_1 add_1_4 (.a(A[0]), .b(B[0]), .c(1'b0), .S(out_4[0]), .Vai_1(add_1_4_vai_1));
  // Probe on out_4
  // Probe on B
endmodule

module sub_1 (
  input  A,
  input  B,
  input  C,
  output A_2,
  output Vai_1
);

  wire and_1_out, and_2_out, or_1_out, xor_1_out;

  xor xor_1 (xor_1_out, C, B);
  or or_1 (or_1_out, C, B);
  xor xor_2 (A_2, xor_1_out, A);
  and and_1 (and_1_out, or_1_out, ~A);  // AND_Gate
  and and_2 (and_2_out, C, B);
  or or_2 (Vai_1, and_1_out, and_2_out);
endmodule

module sub_4 (
  input  [3:0] B,
  input  [3:0] A,
  output out_3,
  output [3:0] out_4
);

  wire sub_1_2_vai_1, sub_1_3_vai_1, sub_1_4_vai_1;

  // Probe on A
  sub_1 sub_1_1 (.A_2(out_4[3]), .Vai_1(out_3), .A(A[3]), .B(B[3]), .C(sub_1_2_vai_1));
  sub_1 sub_1_2 (.A_2(out_4[2]), .Vai_1(sub_1_2_vai_1), .A(A[2]), .B(B[2]), .C(sub_1_3_vai_1));
  sub_1 sub_1_3 (.A_2(out_4[1]), .Vai_1(sub_1_3_vai_1), .A(A[1]), .B(B[1]), .C(sub_1_4_vai_1));
  sub_1 sub_1_4 (.A_2(out_4[0]), .Vai_1(sub_1_4_vai_1), .A(A[0]), .B(B[0]), .C(1'b0));
  // Probe on out_4
  // Probe on B
endmodule

module rot_esq (
  input  [3:0] abcd,
  input  [1:0] xy,
  output [3:0] ABCD_2
);

  wire and_1_out, and_2_out, and_3_out, and_4_out, and_5_out, and_6_out, and_7_out, and_8_out, and_9_out;

  and and_1 (and_1_out, ~xy[1], ~xy[0], abcd[3]);  // AND_Gate
  and and_2 (and_2_out, ~xy[1], xy[0], abcd[2]);  // AND_Gate
  and and_3 (and_3_out, xy[1], ~xy[0], abcd[1]);  // AND_Gate
  and and_4 (and_4_out, xy[1], xy[0], abcd[0]);
  and and_5 (and_5_out, ~xy[1], ~xy[0], abcd[2]);  // AND_Gate
  and and_6 (and_6_out, ~xy[1], xy[0], abcd[1]);  // AND_Gate
  and and_7 (and_7_out, xy[1], ~xy[0], abcd[0]);  // AND_Gate
  and and_8 (and_8_out, ~xy[1], ~xy[0], abcd[1]);  // AND_Gate
  and and_9 (and_9_out, ~xy[1], xy[0], abcd[0]);  // AND_Gate
  and and_10 (ABCD_2[0], ~xy[1], ~xy[0], abcd[0]);  // AND_Gate
  or or_1 (ABCD_2[3], and_1_out, and_2_out, and_3_out, and_4_out);
  or or_2 (ABCD_2[2], and_5_out, and_6_out, and_7_out);
  or or_3 (ABCD_2[1], and_8_out, and_9_out);
endmodule

module rot_dir (
  input  [3:0] abcd,
  input  [1:0] xy,
  output [3:0] ABCD_2
);

  wire and_1_out, and_2_out, and_3_out, and_4_out, and_5_out, and_6_out, and_7_out, and_8_out, and_9_out;

  and and_1 (and_1_out, ~xy[1], ~xy[0], abcd[0]);  // AND_Gate
  and and_2 (and_2_out, ~xy[1], xy[0], abcd[1]);  // AND_Gate
  and and_3 (and_3_out, xy[1], ~xy[0], abcd[2]);  // AND_Gate
  and and_4 (and_4_out, xy[1], xy[0], abcd[3]);
  and and_5 (and_5_out, ~xy[1], ~xy[0], abcd[1]);  // AND_Gate
  and and_6 (and_6_out, ~xy[1], xy[0], abcd[2]);  // AND_Gate
  and and_7 (and_7_out, xy[1], ~xy[0], abcd[3]);  // AND_Gate
  and and_8 (and_8_out, ~xy[1], ~xy[0], abcd[2]);  // AND_Gate
  and and_9 (and_9_out, ~xy[1], xy[0], abcd[3]);  // AND_Gate
  and and_10 (ABCD_2[3], ~xy[1], ~xy[0], abcd[3]);  // AND_Gate
  or or_1 (ABCD_2[0], and_1_out, and_2_out, and_3_out, and_4_out);
  or or_2 (ABCD_2[1], and_5_out, and_6_out, and_7_out);
  or or_3 (ABCD_2[2], and_8_out, and_9_out);
endmodule

module dec_3x8 (
  input  [2:0] in_1,
  output s0,
  output s1,
  output s2,
  output s3,
  output s4,
  output s5,
  output s6,
  output s7
);

  wire not_1_out, not_2_out, not_3_out, not_4_out, not_5_out, not_6_out, not_7_out, not_8_out, not_9_out,
       not_10_out, not_11_out, not_12_out;

  not not_1 (not_1_out, in_1[2]);
  not not_2 (not_2_out, in_1[1]);
  not not_3 (not_3_out, in_1[0]);
  not not_4 (not_4_out, in_1[2]);
  not not_5 (not_5_out, in_1[1]);
  not not_6 (not_6_out, in_1[2]);
  not not_7 (not_7_out, in_1[0]);
  not not_8 (not_8_out, in_1[2]);
  not not_9 (not_9_out, in_1[1]);
  not not_10 (not_10_out, in_1[0]);
  not not_11 (not_11_out, in_1[1]);
  not not_12 (not_12_out, in_1[0]);
  and and_1 (s7, in_1[2], in_1[1], in_1[0]);
  and and_2 (s0, not_1_out, not_2_out, not_3_out);
  and and_3 (s1, not_4_out, not_5_out, in_1[0]);
  and and_4 (s2, not_6_out, in_1[1], not_7_out);
  and and_5 (s3, not_8_out, in_1[1], in_1[0]);
  and and_6 (s4, in_1[2], not_9_out, not_10_out);
  and and_7 (s5, in_1[2], not_11_out, in_1[0]);
  and and_8 (s6, in_1[2], in_1[1], not_12_out);
endmodule

module buffer (
  input  [3:0] E,
  input  in_2,
  output [3:0] S
);

  assign S[2] = in_2 ? E[2] : 1'bz;  // Controlled_Buffer controlled_buffer_1
  assign S[3] = in_2 ? E[3] : 1'bz;  // Controlled_Buffer controlled_buffer_2
  assign S[1] = in_2 ? E[1] : 1'bz;  // Controlled_Buffer controlled_buffer_3
  assign S[0] = in_2 ? E[0] : 1'bz;  // Controlled_Buffer controlled_buffer_4
endmodule
